// Logisim project 4-Bit Adder.circ as structural Verilog: 1 circuit, main circuit main
module main (
  input  A3,
  input  A2,
  input  A1,
  input  A0,
  input  B0,
  input  B3,
  input  B2,
  input  B1,
  input  M,
  output Cout,
  output S3,
  output S2,
  output S1,
  output S0
);

  wire adder_2_cout, adder_3_cout, adder_4_cout, xor_1_out, xor_2_out, xor_3_out, xor_4_out;

  xor xor_1 (xor_1_out, B3, M);
  Adder #(.width(1)) adder_1 (.a(xor_1_out), .b(A3), .out(S3), .cin(adder_2_cout), .cout(Cout));
  xor xor_2 (xor_2_out, B2, M);
  Adder #(.width(1)) adder_2 (.a(xor_2_out), .b(A2), .out(S2), .cin(adder_3_cout), .cout(adder_2_cout));
  xor xor_3 (xor_3_out, B1, M);
  Adder #(.width(1)) adder_3 (.a(xor_3_out), .b(A1), .out(S1), .cin(adder_4_cout), .cout(adder_3_cout));
  xor xor_4 (xor_4_out, B0, M);
  Adder #(.width(1)) adder_4 (.a(xor_4_out), .b(A0), .out(S0), .cin(M), .cout(adder_4_cout));
endmodule
